// Logisim project 20_BITS_fixed.circ as structural Verilog: 7 circuits, main circuit Datapath
module Datapath (
  input  Reset,
  output Cout,
  output Overflow
);

  wire alu_1_zero_check, alu_control_1_s2, alu_control_1_s3, ALU_Src, BEQ_out, BNE_out, Branch_out,
       Clock_out, control_unit_1_beq, control_unit_1_bne, control_unit_1_j, MemRead, MemToReg, MemWrite,
       not_1_out, RegDst, RegWrite;
  wire [1:0] alu_control_1_s1s0, control_unit_1_alu_op, multiplexer_1_out;
  wire [19:0] adder_1_out, adder_2_out, alu_1_out_10, bit_extender_1_out, multiplexer_2_out,
       multiplexer_3_out, multiplexer_4_out, multiplexer_5_out, PC_q, ram_1_data, registers_1_data_1,
       registers_1_data_2, rom_1_data;

  Clock Clock (.out(Clock_out));
  Register #(.width(20)) PC (.D(multiplexer_4_out), .Q(PC_q), .clk(Clock_out), .clr(Reset));  // open: en
  Adder #(.width(20)) adder_1 (.a(20'h1), .b(PC_q), .out(adder_1_out));  // open: cin, cout
  ROM #(.addrWidth(20), .dataWidth(20)) rom_1 (.addr(PC_q), .data(rom_1_data));  // open: sel
  Multiplexer #(.width(2), .enable("false")) multiplexer_1 (
    .in0(rom_1_data[13:12]), .in1(rom_1_data[11:10]), .out(multiplexer_1_out), .sel(RegDst));
  Control_Unit control_unit_1 (
    .Opcode(rom_1_data[19:16]), .J(control_unit_1_j), .RegDst(RegDst), .ALUSrc(ALU_Src), .MemToReg(MemToReg),
    .RegWrite(RegWrite), .MemRead(MemRead), .MemWrite(MemWrite), .BEQ(control_unit_1_beq),
    .BNE(control_unit_1_bne), .ALU_Op(control_unit_1_alu_op));
  Registers registers_1 (
    .Data_In(multiplexer_5_out), .Write_Address__rd(multiplexer_1_out), .Data_1(registers_1_data_1),
    .Data_2(registers_1_data_2), .Read_Address_1__rs(rom_1_data[15:14]), .RegWrite(RegWrite),
    .Clock(Clock_out), .Read_Address_2__rt(rom_1_data[13:12]));
  assign bit_extender_1_out = {{8{rom_1_data[11]}}, rom_1_data[11:0]};  // Bit_Extender bit_extender_1
  ALU_Control alu_control_1 (
    .Function(rom_1_data[4:0]), .ALU_Op(control_unit_1_alu_op), .S3(alu_control_1_s3), .S2(alu_control_1_s2),
    .S1S0(alu_control_1_s1s0));
  ALU alu_1 (
    .S1S0(alu_control_1_s1s0), .Invert(alu_control_1_s2), .Left_Operand(registers_1_data_1),
    .Right_Operand(multiplexer_2_out), .Zero_Check(alu_1_zero_check), .Over_Flow(Overflow), .Cout(Cout),
    .out_10(alu_1_out_10), .S3(alu_control_1_s3), .Shift(rom_1_data[9:5]));
  Multiplexer #(.width(20), .enable("false")) multiplexer_2 (
    .in0(registers_1_data_2), .in1(bit_extender_1_out), .out(multiplexer_2_out), .sel(ALU_Src));
  Adder #(.width(20)) adder_2 (.a(adder_1_out), .b(bit_extender_1_out), .out(adder_2_out));  // open: cin, cout
  and BNE (BNE_out, control_unit_1_bne, not_1_out);
  not not_1 (not_1_out, alu_1_zero_check);
  and BEQ (BEQ_out, control_unit_1_beq, alu_1_zero_check);
  or Branch (Branch_out, BNE_out, BEQ_out);
  Multiplexer #(.width(20), .enable("false")) multiplexer_3 (
    .in0(adder_1_out), .in1(adder_2_out), .out(multiplexer_3_out), .sel(Branch_out));
  RAM #(.addrWidth(20), .dataWidth(20), .bus("separate")) ram_1 (
    .addr(alu_1_out_10), .din(registers_1_data_2), .data(ram_1_data), .str(MemWrite), .clk(Clock_out),
    .ld(MemRead));  // open: sel, clr
  Multiplexer #(.width(20), .enable("false")) multiplexer_4 (
    .in0(multiplexer_3_out), .in1({adder_1_out[19:16], rom_1_data[15:0]}), .out(multiplexer_4_out),
    .sel(control_unit_1_j));
  Multiplexer #(.width(20), .enable("false")) multiplexer_5 (
    .in0(alu_1_out_10), .in1(ram_1_data), .out(multiplexer_5_out), .sel(MemToReg));

  // Notes on the sheet:
  //   contents of rom_1 (hex, n*v repeats v):
  //   11005 31000 12773 32001 6c02 33002 6c03 33003 6c04 33004 6c05 33005 13000 63003 1426 9c08 f000d
  //   52002 2867 f0011
endmodule

module ALU1Bit (
  input  A,
  input  B,
  input  Invert,
  input  Cin,
  input  [1:0] S1S0,
  output Output,
  output Cout
);

  wire adder_1_out, and_1_out, multiplexer_1_out, multiplexer_2_out, multiplexer_3_out, not_1_out, not_2_out,
       not_3_out, or_1_out;

  not not_1 (not_1_out, B);
  and and_1 (and_1_out, A, B);
  not not_2 (not_2_out, and_1_out);
  or or_1 (or_1_out, A, B);
  not not_3 (not_3_out, or_1_out);
  Multiplexer #(.enable("false")) multiplexer_1 (.in0(B), .in1(not_1_out), .out(multiplexer_1_out), .sel(Invert));
  Multiplexer #(.enable("false")) multiplexer_2 (
    .in0(and_1_out), .in1(not_2_out), .out(multiplexer_2_out), .sel(Invert));
  Multiplexer #(.enable("false")) multiplexer_3 (
    .in0(or_1_out), .in1(not_3_out), .out(multiplexer_3_out), .sel(Invert));
  Adder #(.width(1)) adder_1 (.a(A), .b(multiplexer_1_out), .out(adder_1_out), .cin(Cin), .cout(Cout));
  Multiplexer #(.select(2), .enable("false")) multiplexer_4 (
    .in1(multiplexer_3_out), .in2(multiplexer_2_out), .in3(adder_1_out), .out(Output), .sel(S1S0));  // open: in0
endmodule

module halfALU (
  input  [1:0] S1S0,
  input  Cin,
  input  Invert,
  input  [19:0] Left_Operand,
  input  [19:0] Right_Operand,
  output [19:0] Output,
  output Zero,
  output Overflow,
  output CarryOut
);

  wire alu1bit_1_cout, alu1bit_2_cout, alu1bit_3_cout, alu1bit_4_cout, alu1bit_5_cout, alu1bit_6_cout,
       alu1bit_7_cout, alu1bit_8_cout, alu1bit_9_cout, alu1bit_10_cout, alu1bit_11_cout, alu1bit_12_cout,
       alu1bit_13_cout, alu1bit_14_cout, alu1bit_15_cout, alu1bit_16_cout, alu1bit_17_cout, alu1bit_18_cout,
       alu1bit_19_cout;

  ALU1Bit alu1bit_1 (
    .A(Left_Operand[0]), .B(Right_Operand[0]), .Invert(Invert), .Cin(Cin), .S1S0(S1S0),
    .Cout(alu1bit_1_cout), .Output(Output[0]));
  ALU1Bit alu1bit_2 (
    .A(Left_Operand[1]), .B(Right_Operand[1]), .Invert(Invert), .Cin(alu1bit_1_cout), .S1S0(S1S0),
    .Cout(alu1bit_2_cout), .Output(Output[1]));
  ALU1Bit alu1bit_3 (
    .A(Left_Operand[2]), .B(Right_Operand[2]), .Invert(Invert), .Cin(alu1bit_2_cout), .S1S0(S1S0),
    .Cout(alu1bit_3_cout), .Output(Output[2]));
  ALU1Bit alu1bit_4 (
    .A(Left_Operand[3]), .B(Right_Operand[3]), .Invert(Invert), .Cin(alu1bit_3_cout), .S1S0(S1S0),
    .Cout(alu1bit_4_cout), .Output(Output[3]));
  ALU1Bit alu1bit_5 (
    .A(Left_Operand[4]), .B(Right_Operand[4]), .Invert(Invert), .Cin(alu1bit_4_cout), .S1S0(S1S0),
    .Cout(alu1bit_5_cout), .Output(Output[4]));
  ALU1Bit alu1bit_6 (
    .A(Left_Operand[5]), .B(Right_Operand[5]), .Invert(Invert), .Cin(alu1bit_5_cout), .S1S0(S1S0),
    .Cout(alu1bit_6_cout), .Output(Output[5]));
  ALU1Bit alu1bit_7 (
    .A(Left_Operand[6]), .B(Right_Operand[6]), .Invert(Invert), .Cin(alu1bit_6_cout), .S1S0(S1S0),
    .Cout(alu1bit_7_cout), .Output(Output[6]));
  ALU1Bit alu1bit_8 (
    .A(Left_Operand[7]), .B(Right_Operand[7]), .Invert(Invert), .Cin(alu1bit_7_cout), .S1S0(S1S0),
    .Cout(alu1bit_8_cout), .Output(Output[7]));
  ALU1Bit alu1bit_9 (
    .A(Left_Operand[8]), .B(Right_Operand[8]), .Invert(Invert), .Cin(alu1bit_8_cout), .S1S0(S1S0),
    .Cout(alu1bit_9_cout), .Output(Output[8]));
  ALU1Bit alu1bit_10 (
    .A(Left_Operand[9]), .B(Right_Operand[9]), .Invert(Invert), .Cin(alu1bit_9_cout), .S1S0(S1S0),
    .Cout(alu1bit_10_cout), .Output(Output[9]));
  ALU1Bit alu1bit_11 (
    .A(Left_Operand[10]), .B(Right_Operand[10]), .Invert(Invert), .Cin(alu1bit_10_cout), .S1S0(S1S0),
    .Cout(alu1bit_11_cout), .Output(Output[10]));
  ALU1Bit alu1bit_12 (
    .A(Left_Operand[11]), .B(Right_Operand[11]), .Invert(Invert), .Cin(alu1bit_11_cout), .S1S0(S1S0),
    .Cout(alu1bit_12_cout), .Output(Output[11]));
  ALU1Bit alu1bit_13 (
    .A(Left_Operand[12]), .B(Right_Operand[12]), .Invert(Invert), .Cin(alu1bit_12_cout), .S1S0(S1S0),
    .Cout(alu1bit_13_cout), .Output(Output[12]));
  ALU1Bit alu1bit_14 (
    .A(Left_Operand[13]), .B(Right_Operand[13]), .Invert(Invert), .Cin(alu1bit_13_cout), .S1S0(S1S0),
    .Cout(alu1bit_14_cout), .Output(Output[13]));
  ALU1Bit alu1bit_15 (
    .A(Left_Operand[14]), .B(Right_Operand[14]), .Invert(Invert), .Cin(alu1bit_14_cout), .S1S0(S1S0),
    .Cout(alu1bit_15_cout), .Output(Output[14]));
  ALU1Bit alu1bit_16 (
    .A(Left_Operand[15]), .B(Right_Operand[15]), .Invert(Invert), .Cin(alu1bit_15_cout), .S1S0(S1S0),
    .Cout(alu1bit_16_cout), .Output(Output[15]));
  ALU1Bit alu1bit_17 (
    .A(Left_Operand[16]), .B(Right_Operand[16]), .Invert(Invert), .Cin(alu1bit_16_cout), .S1S0(S1S0),
    .Cout(alu1bit_17_cout), .Output(Output[16]));
  ALU1Bit alu1bit_18 (
    .A(Left_Operand[17]), .B(Right_Operand[17]), .Invert(Invert), .Cin(alu1bit_17_cout), .S1S0(S1S0),
    .Cout(alu1bit_18_cout), .Output(Output[17]));
  ALU1Bit alu1bit_19 (
    .A(Left_Operand[18]), .B(Right_Operand[18]), .Invert(Invert), .Cin(alu1bit_18_cout), .S1S0(S1S0),
    .Cout(alu1bit_19_cout), .Output(Output[18]));
  ALU1Bit alu1bit_20 (
    .A(Left_Operand[19]), .B(Right_Operand[19]), .Invert(Invert), .Cin(alu1bit_19_cout), .S1S0(S1S0),
    .Cout(CarryOut), .Output(Output[19]));
  xor xor_1 (Overflow, alu1bit_19_cout, CarryOut);
  nor nor_1 (Zero, Output[0], Output[1], Output[2], Output[3], Output[4], Output[5], Output[6], Output[7], Output[8], Output[9], Output[10], Output[11], Output[12], Output[13], Output[14], Output[15], Output[16], Output[17], Output[18], Output[19]);
endmodule

// Regisster
module Registers (
  input  [1:0] Read_Address_1__rs,
  input  [19:0] Data_In,
  input  [1:0] Read_Address_2__rt,
  input  RegWrite,
  input  Clock,
  input  [1:0] Write_Address__rd,
  output [19:0] Data_1,
  output [19:0] Data_2
);

  wire and_1_out, and_2_out, and_3_out, and_4_out, decoder_1_out0, decoder_1_out1, decoder_1_out2,
       decoder_1_out3;
  wire [19:0] register_1_q, register_2_q, register_3_q, register_4_q;

  Decoder #(.select(2), .enable("false")) decoder_1 (
    .out0(decoder_1_out0), .out1(decoder_1_out1), .out2(decoder_1_out2), .out3(decoder_1_out3),
    .sel(Write_Address__rd));
  and and_1 (and_1_out, decoder_1_out0, RegWrite);
  and and_2 (and_2_out, decoder_1_out1, RegWrite);
  and and_3 (and_3_out, decoder_1_out2, RegWrite);
  and and_4 (and_4_out, decoder_1_out3, RegWrite);
  Register #(.width(20)) register_1 (.D(Data_In), .en(and_1_out), .Q(register_1_q), .clk(Clock));  // open: clr
  Register #(.width(20)) register_2 (.D(Data_In), .en(and_2_out), .Q(register_2_q), .clk(Clock));  // open: clr
  Register #(.width(20)) register_3 (.D(Data_In), .en(and_3_out), .Q(register_3_q), .clk(Clock));  // open: clr
  Register #(.width(20)) register_4 (.D(Data_In), .en(and_4_out), .Q(register_4_q), .clk(Clock));  // open: clr
  Multiplexer #(.select(2), .width(20), .enable("false")) multiplexer_1 (
    .in0(register_1_q), .in1(register_2_q), .in2(register_3_q), .in3(register_4_q), .out(Data_1),
    .sel(Read_Address_1__rs));
  Multiplexer #(.select(2), .width(20), .enable("false")) multiplexer_2 (
    .in0(register_1_q), .in1(register_2_q), .in2(register_3_q), .in3(register_4_q), .out(Data_2),
    .sel(Read_Address_2__rt));
endmodule

module ALU (
  input  [1:0] S1S0,
  input  Invert,
  input  [19:0] Left_Operand,
  input  [19:0] Right_Operand,
  input  [4:0] Shift,
  input  S3,
  output Zero_Check,
  output Over_Flow,
  output Cout,
  output [19:0] out_10
);

  wire comparator_1_lt;
  wire [1:0] multiplexer_2_out;
  wire [19:0] bit_extender_1_out, demultiplexer_1_out0, demultiplexer_1_out1, halfalu_1_output,
       shifter_1_out, shifter_2_out;

  Demultiplexer #(.width(20), .enable("false")) demultiplexer_1 (
    .out0(demultiplexer_1_out0), .out1(demultiplexer_1_out1), .in(Right_Operand), .sel(S3));
  halfALU halfalu_1 (
    .S1S0(S1S0), .Invert(Invert), .Left_Operand(Left_Operand), .Right_Operand(demultiplexer_1_out0),
    .Cin(Invert), .Output(halfalu_1_output), .Zero(Zero_Check), .Overflow(Over_Flow), .CarryOut(Cout));
  Shifter #(.width(20)) shifter_1 (.in(demultiplexer_1_out1), .\dist (Shift), .out(shifter_1_out));
  Shifter #(.width(20), .shift("lr")) shifter_2 (.in(demultiplexer_1_out1), .\dist (Shift), .out(shifter_2_out));
  Comparator #(.width(20)) comparator_1 (
    .a(Left_Operand), .b(demultiplexer_1_out1), .lt(comparator_1_lt));  // open: gt, eq
  assign bit_extender_1_out = {{19{1'b0}}, comparator_1_lt};  // Bit_Extender bit_extender_1
  Multiplexer #(.select(2), .width(20), .enable("false")) multiplexer_1 (
    .in0(bit_extender_1_out), .in1(shifter_2_out), .in2(shifter_1_out), .in3(halfalu_1_output), .out(out_10),
    .sel(multiplexer_2_out));
  Multiplexer #(.width(2), .enable("false")) multiplexer_2 (.in0(2'b11), .in1(S1S0), .out(multiplexer_2_out), .sel(S3));

  // Other names for the same wires on the sheet: Operation[1:0] = S1S0
endmodule

// AC
module ALU_Control (
  input  [4:0] Function,
  input  [1:0] ALU_Op,
  output S3,
  output S2,
  output [1:0] S1S0
);

  wire and_1_out, and_2_out, and_3_out, and_4_out, and_5_out, and_6_out, and_7_out, and_8_out, not_1_out,
       not_2_out, not_3_out, not_4_out, not_5_out, not_6_out, not_7_out, not_8_out, not_9_out, not_10_out,
       not_11_out, not_12_out;

  not not_1 (not_1_out, ALU_Op[0]);
  not not_2 (not_2_out, Function[2]);
  not not_3 (not_3_out, Function[1]);
  not not_4 (not_4_out, ALU_Op[1]);
  not not_5 (not_5_out, ALU_Op[0]);
  not not_6 (not_6_out, Function[3]);
  not not_7 (not_7_out, Function[2]);
  not not_8 (not_8_out, Function[0]);
  not not_9 (not_9_out, ALU_Op[1]);
  not not_10 (not_10_out, ALU_Op[0]);
  not not_11 (not_11_out, Function[3]);
  not not_12 (not_12_out, Function[1]);
  and and_1 (and_1_out, ALU_Op[1], ALU_Op[0], Function[3]);
  and and_2 (and_2_out, ALU_Op[1], ALU_Op[0], Function[2], Function[1]);
  and and_3 (and_3_out, ALU_Op[1], not_2_out, Function[0]);
  and and_4 (and_4_out, ALU_Op[1], not_3_out, Function[0]);
  and and_5 (and_5_out, not_6_out, not_7_out);
  and and_6 (and_6_out, Function[1], not_8_out);
  and and_7 (and_7_out, not_11_out, not_12_out);
  and and_8 (and_8_out, Function[2], Function[0]);
  or or_1 (S3, and_1_out, and_2_out);
  or or_2 (S2, not_1_out, and_3_out, and_4_out);
  or or_3 (S1S0[1], not_4_out, not_5_out, and_5_out, and_6_out);
  or or_4 (S1S0[0], not_9_out, not_10_out, and_7_out, and_8_out);
endmodule

module Control_Unit (
  input  [3:0] Opcode,
  output J,
  output RegDst,
  output ALUSrc,
  output MemToReg,
  output RegWrite,
  output MemRead,
  output MemWrite,
  output BEQ,
  output BNE,
  output [1:0] ALU_Op
);

  wire ADDI_out, SUBI_out;

  and u_J (J, Opcode[3], Opcode[2], Opcode[1], Opcode[0]);
  and ADDI (ADDI_out, ~Opcode[3], ~Opcode[2], ~Opcode[1], Opcode[0]);  // AND_Gate
  and SUBI (SUBI_out, ~Opcode[3], ~Opcode[2], Opcode[1], ~Opcode[0]);  // AND_Gate
  and sw (MemWrite, ~Opcode[3], ~Opcode[2], Opcode[1], Opcode[0]);  // AND_Gate
  and lw (MemRead, ~Opcode[3], Opcode[2], ~Opcode[1], ~Opcode[0]);  // AND_Gate
  and u_bne (BNE, ~Opcode[3], Opcode[2], Opcode[1], ~Opcode[0]);  // AND_Gate
  and u_beq (BEQ, ~Opcode[3], Opcode[2], ~Opcode[1], Opcode[0]);  // AND_Gate
  and R (RegDst, ~Opcode[3], ~Opcode[2], ~Opcode[1], ~Opcode[0]);  // AND_Gate
  or or_1 (ALU_Op[1], BEQ, SUBI_out, BNE, RegDst);
  or or_2 (ALU_Op[0], MemWrite, ADDI_out, MemRead, RegDst);
  or or_3 (ALUSrc, SUBI_out, MemRead, MemWrite, ADDI_out);
  or or_4 (RegWrite, RegDst, MemRead, SUBI_out, ADDI_out);

  assign MemToReg = MemRead;
endmodule
