// Logisim project 16-bit ALU with equality and overflow check.circ as structural Verilog: 3 circuits, main circuit main
module _1_bit_ALU (
  input  CarryIn,
  input  Operand_A,
  input  Operand_B,
  input  BInvert,
  input  [1:0] Operation,
  output Result,
  output Carry
);

  wire adder_1_out, and_1_out, multiplexer_1_out, not_1_out, or_1_out;

  Multiplexer multiplexer_1 (.in0(Operand_B), .in1(not_1_out), .out(multiplexer_1_out), .sel(BInvert));  // open: en
  not not_1 (not_1_out, Operand_B);
  and and_1 (and_1_out, Operand_A, Operand_B);
  or or_1 (or_1_out, Operand_A, Operand_B);
  Adder #(.width(1)) adder_1 (.a(Operand_A), .b(multiplexer_1_out), .out(adder_1_out), .cin(CarryIn), .cout(Carry));
  Multiplexer #(.select(2)) multiplexer_2 (
    .in0(and_1_out), .in1(or_1_out), .in2(adder_1_out), .out(Result), .sel(Operation));  // open: in3, en
endmodule

module _16_bit_ALU (
  input  CarryIn,
  input  [15:0] Operand_A,
  input  BInvert,
  input  [1:0] Operation,
  input  [15:0] Operand_B,
  output [15:0] Result,
  output ZeroEquality,
  output Overflow,
  output CarryOut
);

  wire n1_bit_alu_1_carry, n1_bit_alu_2_carry, n1_bit_alu_3_carry, n1_bit_alu_4_carry, n1_bit_alu_5_carry,
       n1_bit_alu_6_carry, n1_bit_alu_7_carry, n1_bit_alu_8_carry, n1_bit_alu_9_carry, n1_bit_alu_10_carry,
       n1_bit_alu_11_carry, n1_bit_alu_12_carry, n1_bit_alu_13_carry, n1_bit_alu_14_carry,
       n1_bit_alu_15_carry;

  _1_bit_ALU u_1_bit_alu_1 (
    .Operand_A(Operand_A[0]), .Operand_B(Operand_B[0]), .Result(Result[0]), .Carry(n1_bit_alu_1_carry),
    .CarryIn(CarryIn), .BInvert(BInvert), .Operation(Operation));
  _1_bit_ALU u_1_bit_alu_2 (
    .Operand_A(Operand_A[1]), .Operand_B(Operand_B[1]), .Result(Result[1]), .Carry(n1_bit_alu_2_carry),
    .CarryIn(n1_bit_alu_1_carry), .BInvert(BInvert), .Operation(Operation));
  _1_bit_ALU u_1_bit_alu_3 (
    .Operand_A(Operand_A[2]), .Operand_B(Operand_B[2]), .Result(Result[2]), .Carry(n1_bit_alu_3_carry),
    .CarryIn(n1_bit_alu_2_carry), .BInvert(BInvert), .Operation(Operation));
  _1_bit_ALU u_1_bit_alu_4 (
    .Operand_A(Operand_A[3]), .Operand_B(Operand_B[3]), .Result(Result[3]), .Carry(n1_bit_alu_4_carry),
    .CarryIn(n1_bit_alu_3_carry), .BInvert(BInvert), .Operation(Operation));
  _1_bit_ALU u_1_bit_alu_5 (
    .Operand_A(Operand_A[4]), .Operand_B(Operand_B[4]), .Result(Result[4]), .Carry(n1_bit_alu_5_carry),
    .CarryIn(n1_bit_alu_4_carry), .BInvert(BInvert), .Operation(Operation));
  _1_bit_ALU u_1_bit_alu_6 (
    .Operand_A(Operand_A[5]), .Operand_B(Operand_B[5]), .Result(Result[5]), .Carry(n1_bit_alu_6_carry),
    .CarryIn(n1_bit_alu_5_carry), .BInvert(BInvert), .Operation(Operation));
  _1_bit_ALU u_1_bit_alu_7 (
    .Operand_A(Operand_A[6]), .Operand_B(Operand_B[6]), .Result(Result[6]), .Carry(n1_bit_alu_7_carry),
    .CarryIn(n1_bit_alu_6_carry), .BInvert(BInvert), .Operation(Operation));
  _1_bit_ALU u_1_bit_alu_8 (
    .Operand_A(Operand_A[7]), .Operand_B(Operand_B[7]), .Result(Result[7]), .Carry(n1_bit_alu_8_carry),
    .CarryIn(n1_bit_alu_7_carry), .BInvert(BInvert), .Operation(Operation));
  _1_bit_ALU u_1_bit_alu_9 (
    .Operand_A(Operand_A[8]), .Operand_B(Operand_B[8]), .Result(Result[8]), .Carry(n1_bit_alu_9_carry),
    .CarryIn(n1_bit_alu_8_carry), .BInvert(BInvert), .Operation(Operation));
  _1_bit_ALU u_1_bit_alu_10 (
    .Operand_A(Operand_A[9]), .Operand_B(Operand_B[9]), .Result(Result[9]), .Carry(n1_bit_alu_10_carry),
    .CarryIn(n1_bit_alu_9_carry), .BInvert(BInvert), .Operation(Operation));
  _1_bit_ALU u_1_bit_alu_11 (
    .Operand_A(Operand_A[10]), .Operand_B(Operand_B[10]), .Result(Result[10]), .Carry(n1_bit_alu_11_carry),
    .CarryIn(n1_bit_alu_10_carry), .BInvert(BInvert), .Operation(Operation));
  _1_bit_ALU u_1_bit_alu_12 (
    .Operand_A(Operand_A[11]), .Operand_B(Operand_B[11]), .Result(Result[11]), .Carry(n1_bit_alu_12_carry),
    .CarryIn(n1_bit_alu_11_carry), .BInvert(BInvert), .Operation(Operation));
  _1_bit_ALU u_1_bit_alu_13 (
    .Operand_A(Operand_A[12]), .Operand_B(Operand_B[12]), .Result(Result[12]), .Carry(n1_bit_alu_13_carry),
    .CarryIn(n1_bit_alu_12_carry), .BInvert(BInvert), .Operation(Operation));
  _1_bit_ALU u_1_bit_alu_14 (
    .Operand_A(Operand_A[13]), .Operand_B(Operand_B[13]), .Result(Result[13]), .Carry(n1_bit_alu_14_carry),
    .CarryIn(n1_bit_alu_13_carry), .BInvert(BInvert), .Operation(Operation));
  _1_bit_ALU u_1_bit_alu_15 (
    .Operand_A(Operand_A[14]), .Operand_B(Operand_B[14]), .Result(Result[14]), .Carry(n1_bit_alu_15_carry),
    .CarryIn(n1_bit_alu_14_carry), .BInvert(BInvert), .Operation(Operation));
  _1_bit_ALU u_1_bit_alu_16 (
    .Operand_A(Operand_A[15]), .Operand_B(Operand_B[15]), .Result(Result[15]), .Carry(CarryOut),
    .CarryIn(n1_bit_alu_15_carry), .BInvert(BInvert), .Operation(Operation));
  xor xor_1 (Overflow, n1_bit_alu_15_carry, CarryOut);
  nor nor_1 (ZeroEquality, Result[0], Result[1], Result[2], Result[3], Result[4], Result[5], Result[6], Result[7], Result[8], Result[9], Result[10], Result[11], Result[12], Result[13], Result[14], Result[15]);
endmodule

module main (
  input  [2:0] Operation,
  input  [15:0] Operand_A,
  input  CarryIn,
  input  [15:0] Operand_B,
  output [15:0] Result,
  output ZeroEquality,
  output Overflow,
  output CarryOut
);

  _16_bit_ALU u_16_bit_alu_1 (
    .Operand_A(Operand_A), .Operand_B(Operand_B), .ZeroEquality(ZeroEquality), .Overflow(Overflow),
    .CarryOut(CarryOut), .CarryIn(CarryIn), .BInvert(Operation[2]), .Operation(Operation[1:0]),
    .Result(Result));
endmodule
