// Logisim project Control Unit.circ as structural Verilog: 3 circuits, main circuit main
module main (
);

  ALU_Control alu_control_1 ();  // open: Function_Field, ALU_Op, Operation
endmodule

module Control_Unit (
  input  [3:0] Opcode,
  output J,
  output RegDst,
  output ALUSrc,
  output MemToReg,
  output RegWrite,
  output MemRead,
  output MemWrite,
  output [1:0] ALU_Op
);

  wire ADDI_out, beq_out, bne_out, lw_out, R_out, SUBI_out, sw_out;

  and u_J (J, ~Opcode[3], ~Opcode[2], ~Opcode[1], ~Opcode[0]);  // AND_Gate
  and ADDI (ADDI_out, ~Opcode[3], ~Opcode[2], ~Opcode[1], Opcode[0]);  // AND_Gate
  and SUBI (SUBI_out, ~Opcode[3], ~Opcode[2], Opcode[1], ~Opcode[0]);  // AND_Gate
  and sw (sw_out, ~Opcode[3], ~Opcode[2], Opcode[1], Opcode[0]);  // AND_Gate
  and lw (lw_out, ~Opcode[3], Opcode[2], ~Opcode[1], ~Opcode[0]);  // AND_Gate
  and bne (bne_out, ~Opcode[3], Opcode[2], Opcode[1], ~Opcode[0]);  // AND_Gate
  and beq (beq_out, ~Opcode[3], Opcode[2], ~Opcode[1], Opcode[0]);  // AND_Gate
  and R (R_out, Opcode[3], Opcode[2], Opcode[1], Opcode[0]);
  // OR_Gate or_1 has open pins: out=ALUSrc
  // OR_Gate or_2 has open pins: out=RegWrite

  assign ALU_Op[0] = 1'b0;
endmodule

module ALU_Control (
  input  [3:0] Function_Field,
  input  [1:0] ALU_Op,
  output [2:0] Operation
);

  and and_1 (Operation[2], Function_Field[1], ALU_Op[1]);
  or or_1 (Operation[1], ~Function_Field[2], ~ALU_Op[1]);  // OR_Gate
  and and_2 (Operation[0], Function_Field[0], ALU_Op[1]);
endmodule
